# Fritzing sketch AD9851 (saved by Fritzing 0.9.6b)

parts:
  AD1 = DDS AD9850
  J1 = female pin header, 6 pins [form="♀ (female)"]

nets:
  N1: AD1.CLK, J1.pin4
  N2: AD1.FQ, J1.pin3
  N3: AD1.DATA, J1.pin2
  N4: AD1.GND, J1.pin1

notes:
  D7 D6 D5 D4 ......E R/W RS V0 K A
  Мой LCD WINSTAR WH1602A
  GND
  SD
  FQ_UD
  CK
  PWM
  NC
  +5Vcc

custom parts:
  DDS AD9850: AD9850 DDS Signal Generator Module, frequency range 0 to 40MHz, sine or square wave output, on board 70MHz low pass filter, and 125MHz clock module. https://code.google.com/p/ad9850-arduino/
